# Fritzing sketch Circuit (saved by Fritzing 0.9.4)
stripboards: 1

parts:
  VCC2 = 4 x AAA Battery Mount
  C6 = Electrolytic Capacitor [capacitance=47µF package="100 mil [THT, electrolytic]"]
  U6 = Voltage Regulator - Variable [part_number=LM317 package="TO220 [THT]"]
  C7 = Ceramic Capacitor [capacitance=0.1µF package="100 mil [THT, multilayer]"]
  U7 = attiny85 [package=dip]
  J10 = female pin header, 4 pins [form="♀ (female)"]
  C8 = Ceramic Capacitor [capacitance=0.1nF package="100 mil [THT, multilayer]"]
  R18 = Resistor [tolerance=±5% resistance=10k package=THT]
  R19 = Resistor [tolerance=±5% resistance=10k package=THT]
  Q6 = NPN-Transistor [part_number=2N3904 package="TO92 [THT]"]
  R20 = Resistor [tolerance=±5% resistance=10k package=THT]
  R21 = Resistor [tolerance=±5% resistance=10k package=THT]
  J11 = female pin header, 4 pins [form="♀ (female)"]
  J12 = single row smd female pin header, 2 pins [form="♀ (female)"]
  Q7 = NPN-Transistor [part_number=2N3904 package="TO92 [THT]"]
  R17 = Resistor [tolerance=±5% resistance=68 package=THT]
  R16 = Resistor [tolerance=±5% resistance=330 package=THT]

nets:
  N1: VCC2.-, C6.-, C7.0, U7.Pin_4, J10.pin2, C8.0, Q6.E, J11.pin4, Q7.E, R17.Pin_0
  N2: VCC2.+, C6.+, U6.IN, C7.1, U7.Pin_8, J10.pin1, C8.1, R18.Pin_1, R19.Pin_1
  N3: U6.ADJ, R17.Pin_1, R16.Pin_0
  N4: U6.OUT, J12.pin1, R16.Pin_1
  N5: U7.Pin_2, R19.Pin_0, Q7.C
  N6: U7.Pin_3, R18.Pin_0, Q6.C
  N7: U7.Pin_5, J10.pin4
  N8: U7.Pin_6, J10.pin3
  N9: Q6.B, R21.Pin_0
  N10: R20.Pin_0, Q7.B
  N11: R20.Pin_1, J11.pin2
  N12: R21.Pin_1, J11.pin1
  N13: J11.pin3, J12.pin2

notes:
  Clock
  Digital Caliper
  Push to break switch
  DIO
  GND
  VCC
  TM1637 6 Digit Segment Display
  VCC (1.5v)
  Data
